// Logisim project abhinav 1.c.circ as structural Verilog: 1 circuit, main circuit main
module main (
  input  INPUT_A,
  input  INPUT_A_2,
  input  INPUT_B,
  input  INPUT_B_2,
  input  INPUT_A_3,
  input  INPUT_A_4,
  input  INPUT_B_3,
  input  INPUT_B_4,
  input  INPUT_A_5,
  input  INPUT_A_6,
  input  INPUT_B_5,
  input  INPUT_A_7,
  input  INPUT_B_6,
  output OUTPUT_Y,
  output OUTPUT_Y_2,
  output OUTPUT,
  output OUTPUT_Y_3,
  output OUTPUT_X,
  output OUTPUT_Y_4,
  output OUTPUT_Y_5
);

  and AND (OUTPUT_Y, INPUT_A, INPUT_B);
  or OR (OUTPUT_Y_3, INPUT_A_4, INPUT_B_4);
  not NOT (OUTPUT_Y_4, INPUT_A_6);
  nand NAND (OUTPUT_Y_5, INPUT_A_7, INPUT_B_6);
  nor NOR (OUTPUT_Y_2, INPUT_A_2, INPUT_B_2);
  xor XOR (OUTPUT, INPUT_A_3, INPUT_B_3);
  xnor XNOR (OUTPUT_X, INPUT_A_5, INPUT_B_5);

  // Notes on the sheet:
  //   AND GATE_ABHINAV CHAUDHARY_2100320130007
  //   OR GATE_ABHINAV CHAUDHARY_2100320130007
  //   NOT GATE_ABHINAV CHAUDHARY_2100320130007
  //   NAND GATE_ABHINAV CHAUDHARY_2100320130007
  //   NOR GATE_ABHINAV CHAUDHARY_2100320130007
  //   XOR GATE_ABHINAV CHAUDHARY_2100320130007
  //   XNOR GATE_ABHINAV CHAUDHARY_2100320130007
endmodule
